# Fritzing sketch opamp (saved by Fritzing 0.9.1b)
breadboards: 1

parts:
  U1 = OP482 - Low Power, High Speed JFET Quad Operational Amplifier [part_number=OP482]
  Q1 = Basic FET N-Channel [package="TO220 [THT]"]
  R1 = Resistor [tolerance=±5% resistance=1k package=THT]
  D1 = Zener Diode [breakdown_voltage=4.7V package="300 mil [THT]"]
  R2 = Resistor [tolerance=±5% resistance=10k package=THT]

nets:
  N1: U1.OUTA, Q1.gate
  N2: U1.-INA, R2.Pin_0
  N3: U1.+INA, R1.Pin_0, D1.cathode
  12V: U1.V+, R1.Pin_1
  GND: U1.V-, Q1.source, D1.anode
  Output (R): Q1.drain
  input (R): R2.Pin_1
